# Fritzing sketch Nerf (saved by Fritzing 0.9.2b)
breadboards: 3

parts:
  Part1 = Arduino Uno (Rev3) - ICSP
  R4 = Resistor [tolerance=±5% resistance=220 package="1206 [SMD]"]
  LED4 = smd LED [color="Blue (430nm)" package="0805 [SMD]"]
  LED5 = smd LED [color="Green (555nm)" package="0805 [SMD]"]
  LED6 = smd LED [color="Red (633nm)" package="0805 [SMD]"]
  R5 = Resistor [tolerance=±5% resistance=220 package="1206 [SMD]"]
  R6 = Resistor [tolerance=±5% resistance=220 package="1206 [SMD]"]
  Q1 = TRANSISTOR_NPN [package=to-92]
  R7 = Resistor [tolerance=±5% resistance=1k package="0402 [SMD]"]
  VCC1 = 4 x AAA Battery Mount
  Q2 = TRANSISTOR_NPN [package=to-92]
  R8 = Resistor [tolerance=±5% resistance=1k package="0402 [SMD]"]
  S1 = Reed switch [package=THT]  # not connected
  S2 = Reed switch [package=THT]  # not connected
  J1 = Basic Servo
  VCC2 = Battery block 9V  # not connected
  M1 = DC Motor  # not connected
  M2 = DC Motor  # not connected

nets:
  N1: Part1.D8, R7.Pin_1
  N2: Part1.D9_PWM, R8.Pin_1
  N3: Part1.D10_PWM/SS, J1.pulse
  N4: Part1.D2, LED4.anode
  N5: Part1.D3_PWM, LED5.anode
  N6: Part1.D4, LED6.anode
  N7: Part1.GND, R4.Pin_1, R5.Pin_1, R6.Pin_1, Q1.E, VCC1.-, Q2.E
  N8: R4.Pin_0, LED4.cathode
  N9: LED5.cathode, R5.Pin_0
  N10: LED6.cathode, R6.Pin_0
  N11: Q1.B, R7.Pin_0
  N12: VCC1.+, J1.vcc
  N13: Q2.B, R8.Pin_0
